# Fritzing sketch Final (saved by Fritzing 0.9.3b)
breadboards: 1

parts:
  LED1 = LED - 5mm [color="Red (633nm)" package="5 mm [THT]"]
  LED2 = LED - 5mm [color="Red (633nm)" package="5 mm [THT]"]
  LED3 = LED - 5mm [color="Red (633nm)" package="5 mm [THT]"]
  LED4 = LED - 5mm [color="Red (633nm)" package="5 mm [THT]"]
  LED5 = LED - 5mm [color="Red (633nm)" package="5 mm [THT]"]
  LED6 = LED - 5mm [color="Red (633nm)" package="5 mm [THT]"]
  元件1 = LinkIt 7697
  R1 = Resistor [tolerance=±5% resistance=220 package="2010 [SMD]"]
  R2 = Resistor [tolerance=±5% resistance=220 package="2010 [SMD]"]
  R3 = Resistor [tolerance=±5% resistance=220 package="2010 [SMD]"]
  R4 = Resistor [tolerance=±5% resistance=220 package="2010 [SMD]"]
  R5 = Resistor [tolerance=±5% resistance=220 package="2010 [SMD]"]
  R6 = Resistor [tolerance=±5% resistance=220 package="2010 [SMD]"]
  J1 = Basic Servo  # not connected

nets:
  N1: LED1.cathode, LED2.cathode, LED3.cathode, LED4.cathode, LED5.cathode, LED6.cathode, 元件1.GND
  N2: LED1.anode, R5.Pin_0
  N3: LED2.anode, R6.Pin_0
  N4: LED3.anode, R3.Pin_0
  N5: LED4.anode, R1.Pin_0
  N6: LED5.anode, R2.Pin_0
  N7: LED6.anode, R4.Pin_0
  N8: 元件1.P3, R4.Pin_1
  N9: 元件1.P4, R2.Pin_1
  N10: 元件1.P5, R1.Pin_1
  N11: 元件1.P15, R5.Pin_1
  N12: 元件1.P16, R6.Pin_1
  N13: 元件1.P17, R3.Pin_1

custom parts:
  LinkIt 7697: LinkIt 7697 is an IoT development board based on MT7697, supporting Wi-Fi and Bluetooth Low Energy connectivity.
